// Logisim project FSingle.circ as structural Verilog: 16 circuits, main circuit ALU
module main (
);

  wire ALUSrc, BF, clock_1_out, EnMem, ExtOp, Jsel, MemWr_Re, pccontrol_1_branch, pccontrol_1_out_6, PCsrc,
       RegDst, RegWr, WBdata, ZeroFlag;
  wire [1:0] ALUSel, ext_1_out_3, multiplexer_3_out, OPCode;
  wire [2:0] Jump, multiplexer_1_out, multiplexer_2_out, Rw;
  wire [4:0] OP;
  wire [10:0] rom_1_data;
  wire [15:0] branchextender_1_out_3, jump_branch_1_out_6, jumpextender_1_out_3, PC, registers_1_busa;
  wire [31:0] alu_1_out, datamem_1_out_6, multiplexer_4_out, multiplexer_5_out, multiplexer_6_out, PC32,
       registers_1_busb;
  wire [31:2] ext_1_out_3_2;
  wire [31:16] registers_1_busa_2;

  JUMP_BRANCH jump_branch_1 (
    .in_1(branchextender_1_out_3), .in_2(registers_1_busa), .in_3(jumpextender_1_out_3),
    .in_4(jumpextender_1_out_3), .in_5(Jump), .out_6(jump_branch_1_out_6));
  BranchExtender branchextender_1 (.in_1({Rw, rom_1_data[1:0]}), .in_2(PC), .out_3(branchextender_1_out_3));
  JumpExtender jumpextender_1 (
    .in_1({rom_1_data[10:5], Rw, rom_1_data[1:0]}), .in_2(PC[15:11]), .out_3(jumpextender_1_out_3));
  PC pc_1 (.in_1(jump_branch_1_out_6), .in_2(PCsrc), .out_4(PC), .in_3(clock_1_out));
  Clock clock_1 (.out(clock_1_out));
  PCcontrol pccontrol_1 (
    .in_1(OP), .in_2(ZeroFlag), .in_3(BF), .Branch(pccontrol_1_branch), .out_5(Jump),
    .out_6(pccontrol_1_out_6));
  ROM #(.addrWidth(16), .dataWidth(16)) rom_1 (
    .addr(PC), .data({OP, rom_1_data[10:5], Rw, rom_1_data[1:0]}));  // open: sel
  or or_1 (PCsrc, pccontrol_1_branch, pccontrol_1_out_6);
  Multiplexer #(.width(3), .enable("false")) multiplexer_1 (
    .in0(Rw), .in1(3'b111), .out(multiplexer_1_out), .sel(Jump[2]));
  Multiplexer #(.width(3), .enable("false")) multiplexer_2 (
    .in0(rom_1_data[7:5]), .in1(multiplexer_1_out), .out(multiplexer_2_out), .sel(RegDst));
  Ext ext_1 (.in_2({Rw, rom_1_data[1:0]}), .out_3({ext_1_out_3_2, ext_1_out_3}), .in_1(ExtOp));
  Registers registers_1 (
    .BusW(multiplexer_6_out), .RA(rom_1_data[10:8]), .RW(multiplexer_2_out), .RegWrite(RegWr),
    .RB(rom_1_data[7:5]), .BusA({registers_1_busa_2, registers_1_busa}), .BusB(registers_1_busb),
    .in_6(clock_1_out));
  assign PC32 = {{16{1'b0}}, PC};  // Bit_Extender bit_extender_1
  MainControl maincontrol_1 (
    .in_1(OP), .RegDst(RegDst), .RegWr(RegWr), .ExtOp(ExtOp), .ALUSel(ALUSrc), .MemRd(EnMem),
    .MemWr(MemWr_Re), .WBdata(WBdata), .Jsel(Jsel));
  Multiplexer #(.width(2), .enable("false")) multiplexer_3 (
    .in0(OPCode), .in1(ext_1_out_3), .out(multiplexer_3_out), .sel(RegDst));
  Multiplexer #(.width(32), .enable("false")) multiplexer_4 (
    .in0({registers_1_busa_2, registers_1_busa}), .in1(PC32), .out(multiplexer_4_out), .sel(Jsel));
  Multiplexer #(.width(32), .enable("false")) multiplexer_5 (
    .in0(registers_1_busb), .in1({ext_1_out_3_2, ext_1_out_3}), .out(multiplexer_5_out), .sel(ALUSrc));
  ALU alu_1 (
    .A(multiplexer_4_out), .B(multiplexer_5_out), .in_4(multiplexer_3_out), .Out(alu_1_out), .ALUSel(ALUSel),
    .zero_flag(ZeroFlag), .branch_flag(BF));
  Multiplexer #(.width(32), .enable("false")) multiplexer_6 (
    .in0(alu_1_out), .in1(datamem_1_out_6), .out(multiplexer_6_out), .sel(WBdata));
  ALUControl alucontrol_1 (.in_1(OP), .ALUSel(ALUSel), .OpCode(OPCode));
  DataMem datamem_1 (
    .in_1(registers_1_busb), .in_2(alu_1_out[19:0]), .in_4(MemWr_Re), .out_6(datamem_1_out_6),
    .in_5(clock_1_out), .in_3(EnMem));

  // Other names for the same wires on the sheet: PC_5[4:0] = PC[15:11]

  // Notes on the sheet:
  //   contents of rom_1 (hex, n*v repeats v):
  //   4023 14a 6161 7382 69a2 6ba2 5bc3 5be7 a820 e803 9347 0 9267 0 8002
  //   func
endmodule

module ALU (
  input  [31:0] A,
  input  [31:0] B,
  input  [1:0] ALUSel,
  input  [1:0] in_4,
  output [31:0] Out,
  output zero_flag,
  output branch_flag
);

  wire [31:0] arithunit_1_out_4, logic_unit_1_out, PC__2_out_2, shifter_1_shifterout;

  Shifter shifter_1 (.Input(A), .ShiftAmount(B[4:0]), .in_3(in_4), .SHifterOut(shifter_1_shifterout));
  PC_2 PC__2 (.in_1(A), .out_2(PC__2_out_2));
  ArithUnit arithunit_1 (
    .out_4(arithunit_1_out_4), .A(A), .B(B), .in_3(in_4), .branch_flag(branch_flag), .Zero_Flag(zero_flag));
  Logic_Unit logic_unit_1 (.in_A(A), .in_B(B), .Out(logic_unit_1_out), .OPCode(in_4));
  Multiplexer #(.select(2), .width(32), .enable("false")) multiplexer_1 (
    .in0(shifter_1_shifterout), .in1(PC__2_out_2), .in2(arithunit_1_out_4), .in3(logic_unit_1_out),
    .out(Out), .sel(ALUSel));

  // Other names for the same wires on the sheet: Opcode[1:0] = in_4

  // Notes on the sheet:
  //   1
endmodule

module Shifter (
  input  [31:0] Input,
  input  [4:0] ShiftAmount,
  input  [1:0] in_3,
  output [31:0] SHifterOut
);

  wire [4:0] demultiplexer_1_out0, demultiplexer_1_out1, demultiplexer_1_out2, demultiplexer_1_out3;
  wire [31:0] shifter_1_out, shifter_2_out, shifter_3_out, shifter_4_out;

  Demultiplexer #(.select(2), .width(5), .enable("false")) demultiplexer_1 (
    .out0(demultiplexer_1_out0), .out1(demultiplexer_1_out1), .out2(demultiplexer_1_out2),
    .out3(demultiplexer_1_out3), .in(ShiftAmount), .sel(in_3));
  Shifter_part #(.width(32)) shifter_1 (.in(Input), .\dist (demultiplexer_1_out0), .out(shifter_1_out));
  Shifter_part #(.width(32), .shift("lr")) shifter_2 (.in(Input), .\dist (demultiplexer_1_out1), .out(shifter_2_out));
  Shifter_part #(.width(32), .shift("ar")) shifter_3 (.in(Input), .\dist (demultiplexer_1_out2), .out(shifter_3_out));
  Shifter_part #(.width(32), .shift("rr")) shifter_4 (.in(Input), .\dist (demultiplexer_1_out3), .out(shifter_4_out));
  Multiplexer #(.select(2), .width(32), .enable("false")) multiplexer_1 (
    .in0(shifter_1_out), .in1(shifter_2_out), .in2(shifter_3_out), .in3(shifter_4_out), .out(SHifterOut),
    .sel(in_3));

  // Other names for the same wires on the sheet: Operation[1:0] = in_3

  // Notes on the sheet:
  //   SLL
  //   SRL
  //   SRA
  //   ROR
endmodule

module ArithUnit (
  input  [31:0] A,
  input  [31:0] B,
  input  [1:0] in_3,
  output [31:0] out_4,
  output Zero_Flag,
  output branch_flag
);

  wire [31:0] adder_1_out, adder_2_out, bit_extender_1_out, bit_extender_2_out, negator_1_out;

  Comparator #(.width(32)) comparator_1 (.a(A), .b(B), .eq(Zero_Flag), .lt(branch_flag));  // open: gt
  Negator #(.width(32)) negator_1 (.in(A), .out(negator_1_out));
  Adder #(.width(32)) adder_1 (.a(A), .b(B), .out(adder_1_out));  // open: cin, cout
  Adder #(.width(32)) adder_2 (.a(negator_1_out), .b(B), .out(adder_2_out));  // open: cin, cout
  assign bit_extender_1_out = {{31{1'b0}}, Zero_Flag};  // Bit_Extender bit_extender_1
  assign bit_extender_2_out = {{31{1'b0}}, branch_flag};  // Bit_Extender bit_extender_2
  Multiplexer #(.select(2), .width(32), .enable("false")) multiplexer_1 (
    .in0(adder_1_out), .in1(adder_2_out), .in2(bit_extender_1_out), .in3(bit_extender_2_out), .out(out_4),
    .sel(in_3));
endmodule

module Logic_Unit (
  input  [31:0] in_A,
  input  [31:0] in_B,
  input  [1:0] OPCode,
  output [31:0] Out
);

  wire [31:0] AND_out, CAND_out, OR_out, XOR_out;

  assign AND_out = in_A & in_B;  // AND_Gate AND, 32 bits wide
  assign OR_out = in_A | in_B;  // OR_Gate OR, 32 bits wide
  assign XOR_out = in_A ^ in_B;  // XOR_Gate XOR, 32 bits wide
  assign CAND_out = ~AND_out;  // NOT_Gate CAND, 32 bits wide
  Multiplexer #(.select(2), .width(32), .enable("false")) multiplexer_1 (
    .in0(AND_out), .in1(CAND_out), .in2(OR_out), .in3(XOR_out), .out(Out), .sel(OPCode));
endmodule

module Registers (
  input  [2:0] RA,
  input  [31:0] BusW,
  input  [2:0] RW,
  input  RegWrite,
  input  [2:0] RB,
  input  in_6,
  output [31:0] BusA,
  output [31:0] BusB
);

  wire and_1_out, and_2_out, and_3_out, and_4_out, and_5_out, and_6_out, and_7_out, decoder_1_out1,
       decoder_1_out2, decoder_1_out3, decoder_1_out4, decoder_1_out5, decoder_1_out6, decoder_1_out7;
  wire [31:0] R0_q, R1_q, R2_q, R3_q, R4_q, R5_q, R6_q, R7_q;

  Decoder #(.select(3), .enable("false")) decoder_1 (
    .out1(decoder_1_out1), .out2(decoder_1_out2), .out3(decoder_1_out3), .out4(decoder_1_out4),
    .out5(decoder_1_out5), .out6(decoder_1_out6), .out7(decoder_1_out7), .sel(RW));  // open: out0
  and and_1 (and_1_out, decoder_1_out1, RegWrite);
  and and_2 (and_2_out, decoder_1_out2, RegWrite);
  and and_3 (and_3_out, decoder_1_out3, RegWrite);
  and and_4 (and_4_out, decoder_1_out4, RegWrite);
  and and_5 (and_5_out, decoder_1_out5, RegWrite);
  and and_6 (and_6_out, decoder_1_out6, RegWrite);
  and and_7 (and_7_out, decoder_1_out7, RegWrite);
  Register #(.width(32)) R0 (.D({32{1'b0}}), .Q(R0_q), .clk(in_6));  // open: en, clr
  Register #(.width(32)) R1 (.D(BusW), .en(and_1_out), .Q(R1_q), .clk(in_6));  // open: clr
  Register #(.width(32)) R2 (.D(BusW), .en(and_2_out), .Q(R2_q), .clk(in_6));  // open: clr
  Register #(.width(32)) R3 (.D(BusW), .en(and_3_out), .Q(R3_q), .clk(in_6));  // open: clr
  Register #(.width(32)) R4 (.D(BusW), .en(and_4_out), .Q(R4_q), .clk(in_6));  // open: clr
  Register #(.width(32)) R5 (.D(BusW), .en(and_5_out), .Q(R5_q), .clk(in_6));  // open: clr
  Register #(.width(32)) R6 (.D(BusW), .en(and_6_out), .Q(R6_q), .clk(in_6));  // open: clr
  Register #(.width(32)) R7 (.D(BusW), .en(and_7_out), .Q(R7_q), .clk(in_6));  // open: clr
  Multiplexer #(.select(3), .width(32), .enable("false")) multiplexer_1 (
    .in0(R0_q), .in1(R1_q), .in2(R2_q), .in3(R3_q), .in4(R4_q), .in5(R5_q), .in6(R6_q), .in7(R7_q),
    .out(BusA), .sel(RA));
  Multiplexer #(.select(3), .width(32), .enable("false")) multiplexer_2 (
    .in0(R0_q), .in1(R1_q), .in2(R2_q), .in3(R3_q), .in4(R4_q), .in5(R5_q), .in6(R6_q), .in7(R7_q),
    .out(BusB), .sel(RB));
endmodule

module PC (
  input  [15:0] in_1,
  input  in_2,
  input  in_3,
  output [15:0] out_4
);

  wire multiplexer_1_out, not_1_out, not_2_out;

  Multiplexer #(.enable("false")) multiplexer_1 (.in0(1'b0), .in1(not_1_out), .out(multiplexer_1_out), .sel(in_2));
  not not_1 (not_1_out, 1'b0);
  not not_2 (not_2_out, multiplexer_1_out);
  Counter #(.width(16), .max('hffff)) counter_1 (
    .load(multiplexer_1_out), .D(in_1), .count(not_2_out), .Q(out_4), .clk(in_3));  // open: carry, clr
endmodule

module DataMem (
  input  [31:0] in_1,
  input  [19:0] in_2,
  input  in_3,
  input  in_4,
  input  in_5,
  output [31:0] out_6
);

  wire not_1_out;
  wire [31:0] controlled_buffer_1_out;

  assign controlled_buffer_1_out = not_1_out ? in_1 : 32'bz;  // Controlled_Buffer controlled_buffer_1
  not not_1 (not_1_out, in_4);
  RAM #(.addrWidth(20), .dataWidth(32)) ram_1 (
    .addr(in_2), .data(controlled_buffer_1_out), .sel(in_3), .clk(in_5), .ld(in_4));  // open: clr
  assign out_6 = in_4 ? controlled_buffer_1_out : 32'bz;  // Controlled_Buffer controlled_buffer_2
endmodule

module MainControl (
  input  [4:0] in_1,
  output RegDst,
  output RegWr,
  output ExtOp,
  output ALUSel,
  output MemRd,
  output MemWr,
  output WBdata,
  output Jsel
);

  ROM #(.addrWidth(5)) rom_1 (
    .addr(in_1), .data({Jsel, WBdata, MemWr, MemRd, ALUSel, ExtOp, RegWr, RegDst}));  // open: sel

  // Notes on the sheet:
  //   contents of rom_1 (hex, n*v repeats v):
  //   3 3 4*a 10*e 4 4 4 2c 7e 1c 5*0 8a 0 83
endmodule

module ALUControl (
  input  [4:0] in_1,
  output [1:0] ALUSel,
  output [1:0] OpCode
);

  ROM #(.addrWidth(5), .dataWidth(4)) rom_1 (.addr(in_1), .data({OpCode, ALUSel}));  // open: sel

  // Notes on the sheet:
  //   contents of rom_1 (hex, n*v repeats v):
  //   3 2 0 0 3 7 b f 2 6 a e 0 4 8 c 4*0 2 2 5*0 1 0 1
endmodule

module PCcontrol (
  input  [4:0] in_1,
  input  in_2,
  input  in_3,
  output Branch,
  output [2:0] out_5,
  output out_6
);

  wire and_1_out, and_2_out, and_3_out, and_4_out, decoder_1_out16, decoder_1_out17, decoder_1_out18,
       decoder_1_out19, not_1_out, not_2_out;

  Decoder #(.select(5), .enable("false")) decoder_1 (
    .out16(decoder_1_out16), .out17(decoder_1_out17), .out18(decoder_1_out18), .out19(decoder_1_out19),
    .out27(out_5[0]), .out28(out_5[1]), .out29(out_5[2]), .sel(in_1));  // open: out0, out1, out2, out3, out4, out5, out6, out7, out8, out9, out10, out11, out12, out13, out14, out15, out20, out21, out22, out23, out24, out25, out26, out30, out31
  not not_1 (not_1_out, in_2);
  not not_2 (not_2_out, in_3);
  and and_1 (and_1_out, in_2, decoder_1_out16);
  and and_2 (and_2_out, not_1_out, decoder_1_out17);
  and and_3 (and_3_out, decoder_1_out18, in_3);
  and and_4 (and_4_out, not_2_out, decoder_1_out19);
  or or_1 (Branch, and_1_out, and_2_out, and_3_out, and_4_out);
  or or_2 (out_6, out_5[0], out_5[1], out_5[2]);

  // Other names for the same wires on the sheet: BranchFlag = in_3; ZeroFlag = in_2
endmodule

module JumpExtender (
  input  [10:0] in_1,
  input  [4:0] in_2,
  output [15:0] out_3
);

  wire [15:0] bit_extender_1_out, bit_extender_2_out;

  assign bit_extender_1_out = {{5{1'b0}}, in_1};  // Bit_Extender bit_extender_1
  assign bit_extender_2_out = {{11{1'b0}}, in_2};  // Bit_Extender bit_extender_2
  assign out_3 = bit_extender_1_out | bit_extender_2_out;  // OR_Gate or_1, 16 bits wide
endmodule

module BranchExtender (
  input  [4:0] in_1,
  input  [15:0] in_2,
  output [15:0] out_3
);

  wire [15:0] adder_1_out, adder_2_out, bit_extender_1_out, negator_1_out, negator_2_out;

  assign bit_extender_1_out = {{11{in_1[4]}}, in_1};  // Bit_Extender bit_extender_1
  Adder #(.width(16)) adder_1 (.a(in_2), .b({16{1'b0}}), .out(adder_1_out), .cin(1'b1));  // open: cout
  Negator #(.width(16)) negator_1 (.in(bit_extender_1_out), .out(negator_1_out));
  Adder #(.width(16)) adder_2 (.a(negator_1_out), .b(adder_1_out), .out(adder_2_out));  // open: cin, cout
  Negator #(.width(16)) negator_2 (.in(adder_2_out), .out(negator_2_out));
  Adder #(.width(16)) adder_3 (.a(negator_2_out), .b(adder_1_out), .out(out_3));  // open: cin, cout
endmodule

module Ext (
  input  in_1,
  input  [4:0] in_2,
  output [31:0] out_3
);

  wire [31:0] bit_extender_1_out, bit_extender_2_out;

  assign bit_extender_1_out = {{27{1'b0}}, in_2};  // Bit_Extender bit_extender_1
  assign bit_extender_2_out = {{27{in_2[4]}}, in_2};  // Bit_Extender bit_extender_2
  Multiplexer #(.width(32), .enable("false")) multiplexer_1 (
    .in0(bit_extender_1_out), .in1(bit_extender_2_out), .out(out_3), .sel(in_1));
endmodule

module JUMP_BRANCH (
  input  [15:0] in_1,
  input  [15:0] in_2,
  input  [15:0] in_3,
  input  [15:0] in_4,
  input  [2:0] in_5,
  output [15:0] out_6
);

  Multiplexer #(.select(3), .width(16), .enable("false")) multiplexer_1 (
    .in0(in_1), .in1(in_2), .in2(in_3), .in4(in_4), .out(out_6), .sel(in_5));  // open: in3, in5, in6, in7

  // Notes on the sheet:
  //   Branch
  //   JALR
  //   J
  //   JAL
endmodule

module PC_2 (
  input  [31:0] in_1,
  output [31:0] out_2
);

  Adder #(.width(32)) adder_1 (.a(in_1), .b(32'h2), .out(out_2));  // open: cin, cout
endmodule
